# Fritzing sketch twe-analoginput (saved by Fritzing 0.9.2b)
breadboards: 1

parts:
  IC1 = TWE-Lite DIP
  R1 = Trimmer Potentiometer [maximum_resistance=10kΩ package=THT]

nets:
  N1: IC1.ADC1, R1.wiper
