# Fritzing sketch twe-button (saved by Fritzing 0.9.2b)
breadboards: 1

parts:
  IC1 = TWE-Lite DIP
  R1 = Resistor [tolerance=±5% resistance=330 package=THT]
  LED1 = LED - 5mm [color="Green (565nm)" current=20mA package="5 mm [THT]"]
  R2 = Resistor [tolerance=±5% resistance=220 package=THT]
  S1 = Pushbutton [package=THT]

nets:
  N1: IC1.GND#14, R1.Pin_1, R2.Pin_1
  N2: IC1.DIO13, LED1.anode
  N3: IC1.DIO3, R2.Pin_0, S1.leg1
  N4: R1.Pin_0, LED1.cathode
