# Fritzing sketch twe-fading (saved by Fritzing 0.9.2b)
breadboards: 1

parts:
  IC1 = TWE-Lite DIP
  LED1 = LED - 5mm [color="Green (565nm)" package="5 mm [THT]"]
  R1 = Resistor [tolerance=±5% resistance=330 package=THT]

nets:
  N1: IC1.GND#1, R1.Pin_1
  N2: IC1.DIO5, LED1.anode
  N3: LED1.cathode, R1.Pin_0
